# Fritzing sketch Untitled Sketch (saved by Fritzing 0.7.12b)
breadboards: 1

parts:
  Launchpad1 = TI Launchpad MSP430G2
  U1 = Optocoupler [package=THT]
  U2 = Optocoupler [package=THT]
  U3 = Optocoupler [package=THT]
  LED1 = LED - 3mm [color="Red (633nm)" package="3 mm [THT]"]
  LED2 = LED - 3mm [color="Red (633nm)" package="3 mm [THT]"]
  LED3 = LED - 3mm [color="Red (633nm)" package="3 mm [THT]"]
  TRS1 = Audio Jack (TRS) 3.5mm [part_number=Camera package="4Ucon 08780 [THT]"]
  TRS2 = Audio Jack (TRS) 3.5mm [part_number=Flash package="4Ucon 08780 [THT]"]
  TRS3 = Audio Jack (TRS) 3.5mm [part_number=Valve package="4Ucon 08780 [THT]"]
  Q1 = NPN-Transistor [package="SOT-23 [SMD]"]
  R1 = Resistor [tolerance=±5% resistance=6.8k package=THT]
  R2 = Resistor [tolerance=±5% resistance=68k package=THT]
  D1 = Rectifier Diode [part_number=1N4001 package="300 mil [THT]"]
  R3 = Resistor [tolerance=±5% resistance=330 package=THT]
  R4 = Resistor [tolerance=±5% resistance=330 package=THT]
  R5 = Resistor [tolerance=±5% resistance=330 package=THT]
  D2 = Rectifier Diode [part_number=1N4001 package="300 mil [THT]"]
  DC_Power1 = DC Power [voltage=12]

nets:
  N1: Launchpad1.p11, LED3.cathode, R3.Pin_1
  N2: Launchpad1.p12, LED2.cathode, R4.Pin_1
  N3: Launchpad1.p13, LED1.cathode, R5.Pin_1
  N4: Launchpad1.p20, U1.Pin_1, U2.Pin_1, U3.Pin_1, LED1.anode, LED2.anode, LED3.anode
  N5: U1.Pin_2, R5.Pin_0
  N6: U1.Pin_4, TRS1.Sleeve
  N7: U1.Pin_5, TRS1.Tip, D2.cathode
  N8: U2.Pin_2, R4.Pin_0
  N9: U2.Pin_4, TRS2.Sleeve
  N10: U2.Pin_5, TRS2.Tip
  N11: U3.Pin_2, R3.Pin_0
  N12: U3.Pin_4, D1.anode, DC_Power1.GND
  N13: U3.Pin_5, R1.Pin_1
  N14: TRS1.Ring, D2.anode
  N15: TRS3.Sleeve, Q1.1
  N16: TRS3.Tip, D1.cathode
  N17: Q1.2, R2.Pin_1, DC_Power1.V+
  N18: Q1.0, R1.Pin_0, R2.Pin_0
